// Logisim project TTL-Computer.circ as structural Verilog: 6 circuits, main circuit main
module main (
  input  STK_INC,
  input  nC_DATA_OUT,
  input  STK_DEC,
  input  nC_DATA_IN,
  input  nSTK_RESET,
  input  [7:0] DATA_BUS__IN,
  input  PC_INC,
  input  PC_DEC,
  input  nPC_L_LOAD,
  input  nPC_H_LOAD,
  input  nPC_L_OUT,
  input  nPC_H_OUT,
  input  nD_DATA_OUT,
  input  nALU_A_IN,
  input  nD_DATA_IN,
  input  nALU_B_IN,
  input  ALU_S0,
  input  ALU_S1,
  input  ALU_S2,
  input  ALU_S3,
  input  ALU_M,
  input  ALU_Cn,
  input  nA_DATA_OUT,
  input  nALU_OUT,
  input  nA_DATA_IN,
  input  nIR_DATA_IN,
  input  nB_DATA_OUT,
  input  nB_DATA_IN,
  input  nFLAGS_IN,
  output [7:0] DATA_BUS__OUT,
  output Fgt,
  output Feq,
  output Flt,
  output Fz,
  output Fc
);

  wire clock_1_out;
  wire [3:0] ALU_contents_bus_out, ALU_contents_bus_out_2, Instruction_Register_contents_bus_out,
       Instruction_Register_contents_bus_out_2, Program_Counter_mar_bus_out, Program_Counter_mar_bus_out_2,
       Program_Counter_mar_bus_out_3, Program_Counter_mar_bus_out_4, Register_A_contents_bus_out,
       Register_A_contents_bus_out_2, Register_B_contents_bus_out, Register_B_contents_bus_out_2,
       Register_C_contents_bus_out, Register_C_contents_bus_out_2, Register_D_contents_bus_out,
       Register_D_contents_bus_out_2, Stack_Pointer_mar_bus_out_2, Stack_Pointer_mar_bus_out_3;
  wire [4:0] ALU_fc;
  wire [7:0] Flags_Register_data_bus_out;
  wire [7:5] Flags_Register_contents_bus_out;
  wire [11:0] Stack_Pointer_mar_bus_out;

  Hex_Digit_Display hex_digit_display_1 (.value(DATA_BUS__IN[7:4]));  // open: dp
  Hex_Digit_Display hex_digit_display_2 (.value(DATA_BUS__IN[3:0]));  // open: dp
  Hex_Digit_Display hex_digit_display_3 (.value(Program_Counter_mar_bus_out_4));  // open: dp
  Hex_Digit_Display hex_digit_display_4 (.value(Program_Counter_mar_bus_out_3));  // open: dp
  Hex_Digit_Display hex_digit_display_5 (.value(Register_C_contents_bus_out));  // open: dp
  Hex_Digit_Display hex_digit_display_6 (.value(Register_C_contents_bus_out_2));  // open: dp
  Register Register_C (
    .CLOCK(clock_1_out), .nDATA_OUT(nC_DATA_OUT), .nDATA_IN(nC_DATA_IN),
    .CONTENTS_BUS_OUT({Register_C_contents_bus_out_2, Register_C_contents_bus_out}),
    .DATA_BUS_OUT(DATA_BUS__IN), .DATA_BUS_IN(DATA_BUS__IN));
  Hex_Digit_Display hex_digit_display_7 (.value(Program_Counter_mar_bus_out));  // open: dp
  Hex_Digit_Display hex_digit_display_8 (.value(Program_Counter_mar_bus_out_2));  // open: dp
  Hex_Digit_Display hex_digit_display_9 (.value(Register_D_contents_bus_out));  // open: dp
  Hex_Digit_Display hex_digit_display_10 (.value(Register_D_contents_bus_out_2));  // open: dp
  Register Register_D (
    .CLOCK(clock_1_out), .nDATA_OUT(nD_DATA_OUT), .nDATA_IN(nD_DATA_IN),
    .CONTENTS_BUS_OUT({Register_D_contents_bus_out_2, Register_D_contents_bus_out}),
    .DATA_BUS_OUT(DATA_BUS__IN), .DATA_BUS_IN(DATA_BUS__IN));
  Hex_Digit_Display hex_digit_display_11 (.value(Register_A_contents_bus_out_2));  // open: dp
  Hex_Digit_Display hex_digit_display_12 (.value(Register_A_contents_bus_out));  // open: dp
  Register Register_A (
    .CLOCK(clock_1_out), .nDATA_OUT(nA_DATA_OUT), .nDATA_IN(nA_DATA_IN),
    .CONTENTS_BUS_OUT({Register_A_contents_bus_out_2, Register_A_contents_bus_out}),
    .DATA_BUS_OUT(DATA_BUS__IN), .DATA_BUS_IN(DATA_BUS__IN));
  Hex_Digit_Display hex_digit_display_13 (.value(Register_B_contents_bus_out_2));  // open: dp
  Hex_Digit_Display hex_digit_display_14 (.value(Register_B_contents_bus_out));  // open: dp
  Register Register_B (
    .CLOCK(clock_1_out), .nDATA_OUT(nB_DATA_OUT), .nDATA_IN(nB_DATA_IN),
    .CONTENTS_BUS_OUT({Register_B_contents_bus_out_2, Register_B_contents_bus_out}),
    .DATA_BUS_OUT(DATA_BUS__IN), .DATA_BUS_IN(DATA_BUS__IN));
  Clock clock_1 (.out(clock_1_out));
  Program_Counter Program_Counter (
    .PC_INC(PC_INC), .PC_DEC(PC_DEC), .CLOCK(clock_1_out), .PC_L_IN(DATA_BUS__IN), .nPC_L_LOAD(nPC_L_LOAD),
    .PC_H_IN(DATA_BUS__IN), .nPC_H_LOAD(nPC_H_LOAD),
    .MAR_BUS_OUT({Program_Counter_mar_bus_out_4, Program_Counter_mar_bus_out_3, Program_Counter_mar_bus_out_2, Program_Counter_mar_bus_out}),
    .nPC_L_OUT(nPC_L_OUT), .PC_L_DATA(DATA_BUS__IN), .PC_H_DATA(DATA_BUS__IN), .nPC_H_OUT(nPC_H_OUT));
  Register Flags_Register (
    .CLOCK(clock_1_out), .nDATA_OUT(1'b0), .nDATA_IN(nFLAGS_IN),
    .CONTENTS_BUS_OUT({Flags_Register_contents_bus_out, Fgt, Feq, Flt, Fz, Fc}),
    .DATA_BUS_OUT(Flags_Register_data_bus_out), .DATA_BUS_IN({3'b000, ALU_fc}));
  Stack_Pointer Stack_Pointer (
    .STK_INC(STK_INC), .STK_DEC(STK_DEC), .CLOCK(clock_1_out), .nSTK_RESET(nSTK_RESET),
    .MAR_BUS_OUT({Stack_Pointer_mar_bus_out_3, Stack_Pointer_mar_bus_out[11:8], Stack_Pointer_mar_bus_out_2, Stack_Pointer_mar_bus_out[3:0]}));
  ALU ALU (
    .A(DATA_BUS__IN), .CLOCK(clock_1_out), .nA_IN(nALU_A_IN), .nB_IN(nALU_B_IN), .S3(ALU_S3), .S2(ALU_S2),
    .S1(ALU_S1), .S0(ALU_S0), .M(ALU_M), .Cn(ALU_Cn), .nALU_OUT(nALU_OUT), .Flt(ALU_fc[2]), .Feq(ALU_fc[3]),
    .Fgt(ALU_fc[4]), .Fc(ALU_fc[0]), .CONTENTS_BUS_OUT({ALU_contents_bus_out_2, ALU_contents_bus_out}),
    .Fz(ALU_fc[1]));  // open: ALU_DATA_OUT
  Hex_Digit_Display hex_digit_display_15 (.value(Stack_Pointer_mar_bus_out[11:8]));  // open: dp
  Hex_Digit_Display hex_digit_display_16 (.value(Stack_Pointer_mar_bus_out_3));  // open: dp
  Hex_Digit_Display hex_digit_display_17 (.value(ALU_contents_bus_out));  // open: dp
  Hex_Digit_Display hex_digit_display_18 (.value(ALU_contents_bus_out_2));  // open: dp
  Hex_Digit_Display hex_digit_display_19 (.value(Stack_Pointer_mar_bus_out[3:0]));  // open: dp
  Hex_Digit_Display hex_digit_display_20 (.value(Stack_Pointer_mar_bus_out_2));  // open: dp
  Hex_Digit_Display hex_digit_display_21 (.value(Instruction_Register_contents_bus_out_2));  // open: dp
  DotMatrix #(.matrixcols(6), .matrixrows(1), .dotshape("circle")) dotmatrix_1 (
    .col0(Instruction_Register_contents_bus_out_2[1]), .col1(Instruction_Register_contents_bus_out_2[0]),
    .col2(Instruction_Register_contents_bus_out[3]), .col3(Instruction_Register_contents_bus_out[2]),
    .col4(Instruction_Register_contents_bus_out[1]), .col5(Instruction_Register_contents_bus_out[0]));
  Hex_Digit_Display hex_digit_display_22 (.value(Instruction_Register_contents_bus_out));  // open: dp
  Register Instruction_Register (
    .CLOCK(clock_1_out), .nDATA_OUT(1'b0), .nDATA_IN(nIR_DATA_IN),
    .CONTENTS_BUS_OUT({Instruction_Register_contents_bus_out_2, Instruction_Register_contents_bus_out}),
    .DATA_BUS_IN(DATA_BUS__IN));  // open: DATA_BUS_OUT

  assign DATA_BUS__OUT = DATA_BUS__IN;

  // Notes on the sheet:
  //   ~FLAGS-OUT
  //   Create separate input selector per flag
  //   Flags output
endmodule

module Program_Counter (
  input  PC_INC,
  input  PC_DEC,
  input  CLOCK,
  input  [7:0] PC_L_IN,
  input  nPC_L_OUT,
  input  nPC_L_LOAD,
  input  [7:0] PC_H_IN,
  input  nPC_H_OUT,
  input  nPC_H_LOAD,
  output [7:0] PC_L_DATA,
  output [15:0] MAR_BUS_OUT,
  output [7:0] PC_H_DATA
);

  wire DOWN_nUP, n74191_1_nrco, n74191_2_nrco, n74191_3_nrco, nCLK_EN, nor_2_out;

  nor nor_1 (DOWN_nUP, PC_INC, nor_2_out);
  nor nor_2 (nor_2_out, DOWN_nUP, PC_DEC);
  nor nor_3 (nCLK_EN, PC_INC, PC_DEC);
  _74191 u_74191_1 (
    .nU_D(DOWN_nUP), .CK(CLOCK), .nCTEN(nCLK_EN), .nPL(nPC_L_LOAD), .Q0(MAR_BUS_OUT[0]), .Q1(MAR_BUS_OUT[1]),
    .Q2(MAR_BUS_OUT[2]), .Q3(MAR_BUS_OUT[3]), .D0(PC_L_IN[0]), .D1(PC_L_IN[1]), .D2(PC_L_IN[2]),
    .D3(PC_L_IN[3]), .nRCO(n74191_1_nrco));  // open: TC
  _74191 u_74191_2 (
    .nU_D(DOWN_nUP), .CK(n74191_1_nrco), .nCTEN(nCLK_EN), .nPL(nPC_L_LOAD), .Q0(MAR_BUS_OUT[4]),
    .Q1(MAR_BUS_OUT[5]), .Q2(MAR_BUS_OUT[6]), .Q3(MAR_BUS_OUT[7]), .D0(PC_L_IN[4]), .D1(PC_L_IN[5]),
    .D2(PC_L_IN[6]), .D3(PC_L_IN[7]), .nRCO(n74191_2_nrco));  // open: TC
  _74191 u_74191_3 (
    .nU_D(DOWN_nUP), .CK(n74191_2_nrco), .nCTEN(nCLK_EN), .nPL(nPC_H_LOAD), .Q0(MAR_BUS_OUT[8]),
    .Q1(MAR_BUS_OUT[9]), .Q2(MAR_BUS_OUT[10]), .Q3(MAR_BUS_OUT[11]), .D0(PC_H_IN[0]), .D1(PC_H_IN[1]),
    .D2(PC_H_IN[2]), .D3(PC_H_IN[3]), .nRCO(n74191_3_nrco));  // open: TC
  _74191 u_74191_4 (
    .nU_D(DOWN_nUP), .CK(n74191_3_nrco), .nCTEN(nCLK_EN), .nPL(nPC_H_LOAD), .Q0(MAR_BUS_OUT[12]),
    .Q1(MAR_BUS_OUT[13]), .Q2(MAR_BUS_OUT[14]), .Q3(MAR_BUS_OUT[15]), .D0(PC_H_IN[4]), .D1(PC_H_IN[5]),
    .D2(PC_H_IN[6]), .D3(PC_H_IN[7]));  // open: TC, nRCO
  // IC_74244 ic_74244_1: pin names not known; wires that end beside it: MAR_BUS_OUT[0], MAR_BUS_OUT[1], MAR_BUS_OUT[2], MAR_BUS_OUT[3], MAR_BUS_OUT[4], MAR_BUS_OUT[5], MAR_BUS_OUT[6], MAR_BUS_OUT[7], nPC_L_OUT, nPC_L_OUT, PC_L_DATA[0], PC_L_DATA[1], PC_L_DATA[2], PC_L_DATA[3], PC_L_DATA[4], PC_L_DATA[5], PC_L_DATA[6], PC_L_DATA[7]
  // IC_74244 ic_74244_2: pin names not known; wires that end beside it: MAR_BUS_OUT[8], MAR_BUS_OUT[9], MAR_BUS_OUT[10], MAR_BUS_OUT[11], MAR_BUS_OUT[12], MAR_BUS_OUT[13], MAR_BUS_OUT[14], MAR_BUS_OUT[15], nPC_H_OUT, nPC_H_OUT, PC_H_DATA[0], PC_H_DATA[1], PC_H_DATA[2], PC_H_DATA[3], PC_H_DATA[4], PC_H_DATA[5], PC_H_DATA[6], PC_H_DATA[7]
endmodule

module Sequencer_Instruction_Decoder (
  input  nOE,
  input  RESTART,
  input  LOAD
);

  wire and_1_out, and_3_out, and_4_out, and_5_out, CLOCK_out, dip_7474_1_p1, dip_7474_1_p2, dip_7474_1_p4,
       dip_74161_1_p1, dip_74161_1_p3, dip_74161_1_p5, dip_74161_1_p7, dip_74161_1_p9, dip_74161_1_p13,
       dip_74161_2_p2, dip_74161_2_p9, dip_74161_2_p13, dip_74595_1_p2, dip_74595_1_p6, dip_74595_1_p10,
       dip_74595_2_p6, dip_74595_3_p6, dip_74595_4_p6, dip_74595_5_p6, n74165_1_p1, n74165_1_p2,
       n74165_1_p13, not_1_out, not_3_out, not_4_out, not_6_out, not_7_out, not_8_out, or_1_out, or_2_out;
  wire [2:0] dip_74161_2_p3;
  wire [3:0] dip_74595_1_p7, dip_74595_1_p12, dip_74595_2_p3, dip_74595_2_p8, dip_74595_3_p3, dip_74595_3_p8,
       dip_74595_4_p3, dip_74595_4_p8, dip_74595_5_p3, dip_74595_5_p8, dip_74595_6_p3, dip_74595_6_p8;
  wire [7:0] rom_1_data;

  ROM #(.addrWidth(19)) rom_1 (.addr({{16{1'b0}}, dip_74161_2_p3}), .data(rom_1_data), .sel(1'b1));
  // _74165 74165_1: pin names not known; wires that end beside it: n74165_1_p1, n74165_1_p2, rom_1_data[4], rom_1_data[5], rom_1_data[6], rom_1_data[7], 1'b0, rom_1_data[3], rom_1_data[2], rom_1_data[1], rom_1_data[0], 1'b0, n74165_1_p13
  nor nor_1 (n74165_1_p1, LOAD, and_1_out);
  Hex_Digit_Display hex_digit_display_1 (.value(dip_74595_1_p12));  // open: dp
  Hex_Digit_Display hex_digit_display_2 (.value(dip_74595_1_p7));  // open: dp
  DotMatrix #(.matrixcols(24), .matrixrows(1), .dotshape("circle")) dotmatrix_1 (
    .col0(dip_74595_1_p7[3]), .col1(dip_74595_1_p7[2]), .col2(dip_74595_1_p7[1]), .col3(dip_74595_1_p7[0]),
    .col4(dip_74595_1_p12[3]), .col5(dip_74595_1_p12[2]), .col6(dip_74595_1_p12[1]),
    .col7(dip_74595_1_p12[0]), .col8(dip_74595_2_p3[3]), .col9(dip_74595_2_p3[2]), .col10(dip_74595_2_p3[1]),
    .col11(dip_74595_2_p3[0]), .col12(dip_74595_2_p8[3]), .col13(dip_74595_2_p8[2]),
    .col14(dip_74595_2_p8[1]), .col15(dip_74595_2_p8[0]), .col16(dip_74595_3_p3[3]),
    .col17(dip_74595_3_p3[2]), .col18(dip_74595_3_p3[1]), .col19(dip_74595_3_p3[0]),
    .col20(dip_74595_3_p8[3]), .col21(dip_74595_3_p8[2]), .col22(dip_74595_3_p8[1]), .col23(dip_74595_3_p8[0]));
  // DIP_74595 dip_74595_1: pin names not known; wires that end beside it: dip_74595_1_p7[3], dip_74595_1_p2, dip_74595_1_p7[2], n74165_1_p2, dip_74595_1_p7[1], dip_74595_1_p6, dip_74595_1_p7[0], nOE, dip_74595_1_p12[3], dip_74595_1_p10, dip_74595_1_p12[2], dip_74595_1_p12[0], dip_74595_1_p12[1], dip_74595_1_p10, dip_74595_2_p3[3], dip_74595_1_p2, dip_74595_2_p3[2], n74165_1_p2
  Hex_Digit_Display hex_digit_display_3 (.value(dip_74595_2_p3));  // open: dp
  Hex_Digit_Display hex_digit_display_4 (.value(dip_74595_2_p8));  // open: dp
  // DIP_74595 dip_74595_2: pin names not known; wires that end beside it: dip_74595_2_p3[1], dip_74595_1_p6, dip_74595_2_p3[0], nOE, dip_74595_2_p8[3], dip_74595_2_p6, dip_74595_2_p8[2], dip_74595_2_p8[0], dip_74595_2_p8[1], dip_74595_2_p6, dip_74595_3_p3[3], dip_74595_1_p2, dip_74595_3_p3[2], n74165_1_p2
  Hex_Digit_Display hex_digit_display_5 (.value(dip_74595_3_p3));  // open: dp
  Hex_Digit_Display hex_digit_display_6 (.value(dip_74595_3_p8));  // open: dp
  // DIP_74595 dip_74595_3: pin names not known; wires that end beside it: dip_74595_3_p3[1], dip_74595_1_p6, dip_74595_3_p3[0], nOE, dip_74595_3_p8[3], dip_74595_3_p6, dip_74595_3_p8[2], dip_74595_3_p8[0], dip_74595_3_p8[1], dip_74595_3_p6, dip_74595_4_p3[3], dip_74595_1_p2, dip_74595_4_p3[2], n74165_1_p2
  and and_1 (and_1_out, and_4_out, CLOCK_out);
  Hex_Digit_Display hex_digit_display_7 (.value(dip_74595_4_p3));  // open: dp
  DotMatrix #(.matrixcols(24), .matrixrows(1), .dotshape("circle")) dotmatrix_2 (
    .col0(dip_74595_4_p3[3]), .col1(dip_74595_4_p3[2]), .col2(dip_74595_4_p3[1]), .col3(dip_74595_4_p3[0]),
    .col4(dip_74595_4_p8[3]), .col5(dip_74595_4_p8[2]), .col6(dip_74595_4_p8[1]), .col7(dip_74595_4_p8[0]),
    .col8(dip_74595_5_p3[3]), .col9(dip_74595_5_p3[2]), .col10(dip_74595_5_p3[1]), .col11(dip_74595_5_p3[0]),
    .col12(dip_74595_5_p8[3]), .col13(dip_74595_5_p8[2]), .col14(dip_74595_5_p8[1]),
    .col15(dip_74595_5_p8[0]), .col16(dip_74595_6_p3[3]), .col17(dip_74595_6_p3[2]),
    .col18(dip_74595_6_p3[1]), .col19(dip_74595_6_p3[0]), .col20(dip_74595_6_p8[3]),
    .col21(dip_74595_6_p8[2]), .col22(dip_74595_6_p8[1]), .col23(dip_74595_6_p8[0]));
  nor nor_2 (dip_74595_1_p2, n74165_1_p1, or_1_out);
  Hex_Digit_Display hex_digit_display_8 (.value(dip_74595_4_p8));  // open: dp
  Hex_Digit_Display hex_digit_display_9 (.value(dip_74595_5_p3));  // open: dp
  // DIP_74595 dip_74595_4: pin names not known; wires that end beside it: dip_74595_4_p3[1], dip_74595_1_p6, dip_74595_4_p3[0], nOE, dip_74595_4_p8[3], dip_74595_4_p6, dip_74595_4_p8[2], dip_74595_4_p8[0], dip_74595_4_p8[1], dip_74595_4_p6, dip_74595_5_p3[3], dip_74595_1_p2, dip_74595_5_p3[2], n74165_1_p2
  and and_2 (n74165_1_p2, and_3_out, not_3_out);
  or or_1 (or_1_out, and_4_out, not_1_out);
  and and_3 (and_3_out, or_2_out, CLOCK_out);
  not not_1 (not_1_out, CLOCK_out);
  or or_2 (or_2_out, n74165_1_p1, and_4_out);
  Clock CLOCK (.out(CLOCK_out));
  Hex_Digit_Display hex_digit_display_10 (.value(dip_74595_6_p3));  // open: dp
  Hex_Digit_Display hex_digit_display_11 (.value(dip_74595_5_p8));  // open: dp
  // DIP_74595 dip_74595_5: pin names not known; wires that end beside it: dip_74595_5_p3[1], dip_74595_1_p6, dip_74595_5_p3[0], nOE, dip_74595_5_p8[3], dip_74595_5_p6, dip_74595_5_p8[2], dip_74595_5_p8[0], dip_74595_5_p8[1], dip_74595_5_p6, dip_74595_6_p3[3], dip_74595_1_p2, dip_74595_6_p3[2], n74165_1_p2
  not not_2 (dip_74595_1_p6, n74165_1_p2);
  not not_3 (not_3_out, and_5_out);
  Hex_Digit_Display hex_digit_display_12 (.value(dip_74595_6_p8));  // open: dp
  // DIP_74595 dip_74595_6: pin names not known; wires that end beside it: dip_74595_6_p3[1], dip_74595_1_p6, dip_74595_6_p3[0], nOE, dip_74595_6_p8[3], n74165_1_p13, dip_74595_6_p8[2], dip_74595_6_p8[0], dip_74595_6_p8[1]
  DotMatrix #(.matrixcols(4), .matrixrows(1), .dotshape("circle")) dotmatrix_3 (
    .col0(dip_74161_1_p9), .col1(dip_74161_1_p7), .col2(dip_74161_1_p5), .col3(dip_74161_1_p3));
  and and_4 (and_4_out, dip_74161_1_p3, dip_74161_1_p5, dip_74161_1_p7);
  // DIP_74161 dip_74161_1: pin names not known; wires that end beside it: dip_74161_1_p1, n74165_1_p2, dip_74161_1_p3, 1'b0, dip_74161_1_p5, 1'b0, dip_74161_1_p7, 1'b0, dip_74161_1_p9, 1'b0, 1'b1, 1'b1, dip_74161_1_p13
  or or_3 (dip_74161_1_p1, and_4_out, n74165_1_p1);
  and and_5 (and_5_out, dip_7474_1_p4, not_4_out);
  not not_4 (not_4_out, LOAD);
  not not_5 (dip_74161_1_p13, and_4_out);
  not not_6 (not_6_out, dip_74595_1_p2);
  // Probe on dip_74161_2_p2
  not not_7 (not_7_out, and_4_out);
  not not_8 (not_8_out, CLOCK_out);
  DotMatrix #(.matrixcols(4), .matrixrows(1), .dotshape("circle")) dotmatrix_4 (
    .col0(dip_74161_2_p9), .col1(dip_74161_2_p3[2]), .col2(dip_74161_2_p3[1]), .col3(dip_74161_2_p3[0]));
  // DIP_74161 dip_74161_2: pin names not known; wires that end beside it: not_6_out, dip_74161_2_p2, dip_74161_2_p3[0], 1'b0, dip_74161_2_p3[1], 1'b0, dip_74161_2_p3[2], 1'b0, dip_74161_2_p9, 1'b0, 1'b1, 1'b1, dip_74161_2_p13
  // AND_Gate and_6 has open pins: in1=n74165_1_p2, out=open
  nor nor_3 (dip_74161_2_p2, not_7_out, n74165_1_p2, not_8_out);
  // DIP_7474 dip_7474_1: pin names not known; wires that end beside it: dip_7474_1_p1, dip_7474_1_p2, dip_7474_1_p2, dip_7474_1_p4
  not not_9 (dip_7474_1_p1, LOAD);
  not not_10 (dip_74161_2_p13, RESTART);
  and and_7 (dip_7474_1_p2, dip_74161_2_p3[1], dip_74161_2_p3[2]);

  // Notes on the sheet:
  //   RESTART: pull=down
  //   LOAD: pull=down
  //   nOE: pull=down
  //   CONTROL ROM
  //   contents of rom_1 (hex, n*v repeats v):
  //   a3 b6 3c 1d e9 8f
  //   SH/~LR
  //   ROM DATA
  //   DATA
  //   NEXT_BIT
  //   ~CLR
  //   ~CLR
  //   RCLK
  //   SRCLK
  //   DATA
  //   DATA BIT COUNTER
  //   CLR
  //   NEXT_BIT
  //   DONE
  //   CE
  //   CLR
  //   RESTART
  //   DATA BYTE COUNTER
  //   CE
endmodule

module Register (
  input  [7:0] DATA_BUS_IN,
  input  CLOCK,
  input  nDATA_IN,
  input  nDATA_OUT,
  output [7:0] CONTENTS_BUS_OUT,
  output [7:0] DATA_BUS_OUT
);

  // IC_74377 ic_74377_1: pin names not known; wires that end beside it: CLOCK, nDATA_IN, CONTENTS_BUS_OUT[0], CONTENTS_BUS_OUT[1], CONTENTS_BUS_OUT[2], CONTENTS_BUS_OUT[3], CONTENTS_BUS_OUT[4], CONTENTS_BUS_OUT[5], CONTENTS_BUS_OUT[6], CONTENTS_BUS_OUT[7]
  // IC_74244 ic_74244_1: pin names not known; wires that end beside it: CONTENTS_BUS_OUT[0], CONTENTS_BUS_OUT[1], CONTENTS_BUS_OUT[2], CONTENTS_BUS_OUT[3], CONTENTS_BUS_OUT[4], CONTENTS_BUS_OUT[5], CONTENTS_BUS_OUT[6], CONTENTS_BUS_OUT[7], nDATA_OUT, nDATA_OUT, DATA_BUS_OUT[0], DATA_BUS_OUT[1], DATA_BUS_OUT[2], DATA_BUS_OUT[3], DATA_BUS_OUT[4], DATA_BUS_OUT[5], DATA_BUS_OUT[6], DATA_BUS_OUT[7]
endmodule

module Stack_Pointer (
  input  STK_INC,
  input  STK_DEC,
  input  CLOCK,
  input  nSTK_RESET,
  output [15:0] MAR_BUS_OUT
);

  wire DOWN_nUP, n74191_1_nrco, nCLK_EN, nor_2_out;

  nor nor_1 (DOWN_nUP, STK_INC, nor_2_out);
  nor nor_2 (nor_2_out, DOWN_nUP, STK_DEC);
  nor nor_3 (nCLK_EN, STK_INC, STK_DEC);
  _74191 u_74191_1 (
    .nU_D(DOWN_nUP), .CK(CLOCK), .nCTEN(nCLK_EN), .nPL(nSTK_RESET), .Q0(MAR_BUS_OUT[0]), .Q1(MAR_BUS_OUT[1]),
    .Q2(MAR_BUS_OUT[2]), .Q3(MAR_BUS_OUT[3]), .D0(1'b0), .D1(1'b0), .D2(1'b0), .D3(1'b0), .nRCO(n74191_1_nrco));  // open: TC
  _74191 u_74191_2 (
    .nU_D(DOWN_nUP), .CK(n74191_1_nrco), .nCTEN(nCLK_EN), .nPL(nSTK_RESET), .Q0(MAR_BUS_OUT[4]),
    .Q1(MAR_BUS_OUT[5]), .Q2(MAR_BUS_OUT[6]), .Q3(MAR_BUS_OUT[7]), .D0(1'b0), .D1(1'b0), .D2(1'b0), .D3(1'b0));  // open: TC, nRCO

  assign MAR_BUS_OUT[15:8] = {8{1'b1}};
endmodule

module ALU (
  input  [7:0] A,
  input  CLOCK,
  input  nA_IN,
  input  nB_IN,
  input  S3,
  input  S2,
  input  S1,
  input  S0,
  input  M,
  input  Cn,
  input  nALU_OUT,
  output Flt,
  output Feq,
  output Fgt,
  output [7:0] ALU_DATA_OUT,
  output Fc,
  output [7:0] CONTENTS_BUS_OUT,
  output Fz
);

  wire and_1_out, and_3_out, ic_74377_1_p1, ic_74377_1_p2, ic_74377_1_p3, ic_74377_1_p4, ic_74377_1_p5,
       ic_74377_1_p6, ic_74377_1_p7, ic_74377_1_p8, ic_74377_2_p5, ic_74377_2_p6, ic_74377_2_p7,
       ic_74377_2_p8, ic_74377_2_p9, ic_74377_2_p10, ic_74377_2_p11, ic_74377_2_p12, n74181_1_p18,
       n74181_1_p19, n74181_2_p18, n74181_2_p19, not_2_out, not_3_out;

  // IC_74377 ic_74377_1: pin names not known; wires that end beside it: ic_74377_1_p1, ic_74377_1_p2, ic_74377_1_p3, ic_74377_1_p4, ic_74377_1_p5, ic_74377_1_p6, ic_74377_1_p7, ic_74377_1_p8
  // IC_74377 ic_74377_2: pin names not known; wires that end beside it: CLOCK, nA_IN, CLOCK, nB_IN, ic_74377_2_p5, ic_74377_2_p6, ic_74377_2_p7, ic_74377_2_p8, ic_74377_2_p9, ic_74377_2_p10, ic_74377_2_p11, ic_74377_2_p12
  // _74181 74181_1: pin names not known; wires that end beside it: ic_74377_2_p5, ic_74377_1_p1, S3, S2, S1, S0, Cn, M, CONTENTS_BUS_OUT[0], CONTENTS_BUS_OUT[1], CONTENTS_BUS_OUT[2], ic_74377_1_p2, ic_74377_2_p6, ic_74377_1_p3, ic_74377_2_p7, ic_74377_1_p4, ic_74377_2_p8, n74181_1_p18, n74181_1_p19, CONTENTS_BUS_OUT[3]
  // _74181 74181_2: pin names not known; wires that end beside it: ic_74377_2_p9, ic_74377_1_p5, S3, S2, S1, S0, n74181_1_p18, M, CONTENTS_BUS_OUT[4], CONTENTS_BUS_OUT[5], CONTENTS_BUS_OUT[6], ic_74377_1_p6, ic_74377_2_p10, ic_74377_1_p7, ic_74377_2_p11, ic_74377_1_p8, ic_74377_2_p12, n74181_2_p18, n74181_2_p19, CONTENTS_BUS_OUT[7]
  not not_1 (Fc, n74181_2_p18);
  and and_1 (and_1_out, n74181_1_p18, n74181_2_p18);
  or or_1 (Flt, and_1_out, n74181_2_p18);
  and and_2 (Feq, n74181_1_p19, n74181_2_p19);
  not not_2 (not_2_out, n74181_1_p18);
  not not_3 (not_3_out, n74181_2_p18);
  and and_3 (and_3_out, not_2_out, not_3_out);
  or or_2 (Fgt, and_3_out, not_3_out);
  nor nor_1 (Fz, CONTENTS_BUS_OUT[0], CONTENTS_BUS_OUT[1], CONTENTS_BUS_OUT[2], CONTENTS_BUS_OUT[3], CONTENTS_BUS_OUT[4], CONTENTS_BUS_OUT[5], CONTENTS_BUS_OUT[6], CONTENTS_BUS_OUT[7]);
  // IC_74244 ic_74244_1: pin names not known; wires that end beside it: CONTENTS_BUS_OUT[0], CONTENTS_BUS_OUT[1], CONTENTS_BUS_OUT[2], CONTENTS_BUS_OUT[3], CONTENTS_BUS_OUT[4], CONTENTS_BUS_OUT[5], CONTENTS_BUS_OUT[6], CONTENTS_BUS_OUT[7], nALU_OUT, nALU_OUT, ALU_DATA_OUT[0], ALU_DATA_OUT[1], ALU_DATA_OUT[2], ALU_DATA_OUT[3], ALU_DATA_OUT[4], ALU_DATA_OUT[5], ALU_DATA_OUT[6], ALU_DATA_OUT[7]

  // Notes on the sheet:
  //   M=0   Cn=0   S=0110  (A < B)
  //   M=0   Cn=1   S=0110  (A=B)
  //   M=0   Cn=1   S=0110  (A>B)
endmodule
